// Logisim project FA.circ as structural Verilog: 1 circuit, main circuit main
module main (
  input  Ai,
  input  Bi,
  input  Ci,
  output Ci_1,
  output Si
);

  wire and_1_out, and_2_out, xor_1_out;

  and and_1 (and_1_out, Ai, Bi);
  xor xor_1 (xor_1_out, Ai, Bi);
  and and_2 (and_2_out, Ci, xor_1_out);
  or or_1 (Ci_1, and_1_out, and_2_out);
  xor xor_2 (Si, xor_1_out, Ci);
endmodule
