// Logisim project RAM.circ as structural Verilog: 1 circuit, main circuit main
module main (
  input  [7:0] Address,
  input  [7:0] Input,
  input  CS,
  input  R_W,
  output [7:0] Output
);

  wire not_1_out;
  wire [7:0] ram_1_data;

  RAM #(.bus("asynch")) ram_1 (.addr(Address), .data(ram_1_data), .sel(CS), .ld(R_W));  // open: clr
  assign Output = R_W ? ram_1_data : 8'bz;  // Controlled_Buffer controlled_buffer_1
  assign ram_1_data = not_1_out ? Input : 8'bz;  // Controlled_Buffer controlled_buffer_2
  not not_1 (not_1_out, R_W);
endmodule
