// Logisim project lab3.circ as structural Verilog: 2 circuits, main circuit main
module main (
  input  Ai,
  input  Bi,
  input  Ci,
  output Ci_1,
  output Si
);

  wire and_1_out, and_2_out, xor_1_out;

  and and_1 (and_1_out, Ai, Bi);
  xor xor_1 (xor_1_out, Ai, Bi);
  and and_2 (and_2_out, Ci, xor_1_out);
  or or_1 (Ci_1, and_1_out, and_2_out);
  xor xor_2 (Si, xor_1_out, Ci);
endmodule

module main2 (
  input  \方式控制 ,
  input  B7,
  input  B6,
  input  B5,
  input  B4,
  input  B3,
  input  B2,
  input  B1,
  input  B0,
  input  A7,
  input  A6,
  input  A5,
  input  A4,
  input  A3,
  input  A2,
  input  A1,
  input  A0,
  output \溢出 ,
  output S7,
  output S6,
  output S5,
  output S,
  output S3,
  output S2,
  output S1,
  output S0
);

  wire main_1_ci_1, main_2_ci_1, main_3_ci_1, main_4_ci_1, main_5_ci_1, main_6_ci_1, main_7_ci_1,
       main_8_ci_1, xor_2_out, xor_3_out, xor_4_out, xor_5_out, xor_6_out, xor_7_out, xor_8_out, xor_9_out;

  xor xor_1 (\溢出 , main_1_ci_1, main_2_ci_1);
  xor xor_2 (xor_2_out, B7, \方式控制 );
  main main_1 (.Ai(A7), .Bi(xor_2_out), .Ci(main_2_ci_1), .Ci_1(main_1_ci_1), .Si(S7));
  main main_2 (.Ai(A6), .Bi(xor_3_out), .Ci(main_3_ci_1), .Ci_1(main_2_ci_1), .Si(S6));
  xor xor_3 (xor_3_out, B6, \方式控制 );
  main main_3 (.Ai(A5), .Bi(xor_4_out), .Ci(main_4_ci_1), .Ci_1(main_3_ci_1), .Si(S5));
  xor xor_4 (xor_4_out, B5, \方式控制 );
  main main_4 (.Ai(A4), .Bi(xor_5_out), .Ci(main_5_ci_1), .Ci_1(main_4_ci_1), .Si(S));
  xor xor_5 (xor_5_out, B4, \方式控制 );
  main main_5 (.Ai(A3), .Bi(xor_6_out), .Ci(main_6_ci_1), .Ci_1(main_5_ci_1), .Si(S3));
  xor xor_6 (xor_6_out, B3, \方式控制 );
  xor xor_7 (xor_7_out, B2, \方式控制 );
  main main_6 (.Ai(A2), .Bi(xor_7_out), .Ci(main_7_ci_1), .Ci_1(main_6_ci_1), .Si(S2));
  main main_7 (.Ai(A1), .Bi(xor_8_out), .Ci(main_8_ci_1), .Ci_1(main_7_ci_1), .Si(S1));
  xor xor_8 (xor_8_out, B1, \方式控制 );
  main main_8 (.Ai(A0), .Bi(xor_9_out), .Ci(\方式控制 ), .Ci_1(main_8_ci_1), .Si(S0));
  xor xor_9 (xor_9_out, B0, \方式控制 );
endmodule
