// Logisim project 位扩展.circ as structural Verilog: 1 circuit, main circuit main
module main (
  input  [9:0] in_1,
  input  in_2,
  input  in_3,
  input  in_4,
  input  [7:0] in_5,
  input  [7:0] in_6,
  output [7:0] out_7,
  output [7:0] out_8
);

  wire not_1_out, not_2_out;
  wire [7:0] ram_1_data, ram_2_data;

  Decoder #(.select(2)) decoder_1 (.en(in_4));  // open: out0, out1, out2, out3, sel
  RAM #(.addrWidth(10), .bus("asynch")) ram_1 (.addr(in_1), .data(ram_1_data), .sel(in_2), .ld(in_3));  // open: clr
  assign ram_1_data = not_1_out ? in_5 : 8'bz;  // Controlled_Buffer controlled_buffer_1
  not not_1 (not_1_out, in_3);
  assign out_7 = in_3 ? ram_1_data : 8'bz;  // Controlled_Buffer controlled_buffer_2
  RAM #(.addrWidth(10), .bus("asynch")) ram_2 (.addr(in_1), .data(ram_2_data), .sel(in_2), .ld(in_3));  // open: clr
  assign out_8 = in_3 ? ram_2_data : 8'bz;  // Controlled_Buffer controlled_buffer_3
  assign ram_2_data = not_2_out ? in_6 : 8'bz;  // Controlled_Buffer controlled_buffer_4
  not not_2 (not_2_out, in_3);

  // Notes on the sheet:
  //   Address
endmodule
