// Logisim project 判断输入三位二进制数是否大于等于4.circ as structural Verilog: 1 circuit, main circuit main
module main (
  input  in_1,
  input  [2:0] in_2,
  output out_3
);

  wire decoder_1_out4, decoder_1_out5, decoder_1_out6, decoder_1_out7, not_1_out, not_2_out, not_3_out,
       not_4_out;

  Decoder #(.select(3)) decoder_1 (
    .out4(decoder_1_out4), .out5(decoder_1_out5), .out6(decoder_1_out6), .out7(decoder_1_out7), .sel(in_2),
    .en(in_1));  // open: out0, out1, out2, out3
  not not_1 (not_1_out, decoder_1_out4);
  not not_2 (not_2_out, decoder_1_out5);
  not not_3 (not_3_out, decoder_1_out6);
  not not_4 (not_4_out, decoder_1_out7);
  nand nand_1 (out_3, not_1_out, not_2_out, not_3_out, not_4_out);
endmodule
