// Logisim project 字位扩展.circ as structural Verilog: 1 circuit, main circuit main
module main (
  input  [9:0] in_1,
  input  R_W,
  input  CS,
  input  [1:0] in_4,
  input  [7:0] Input,
  input  [7:0] Input_2,
  output [7:0] High,
  output [7:0] Low
);

  wire decoder_1_out0, decoder_1_out1, decoder_1_out2, decoder_1_out3, not_1_out, not_2_out;
  wire [7:0] ram_1_data, ram_5_data;

  Decoder #(.select(2)) decoder_1 (
    .out0(decoder_1_out0), .out1(decoder_1_out1), .out2(decoder_1_out2), .out3(decoder_1_out3), .sel(in_4),
    .en(CS));
  RAM #(.addrWidth(10), .bus("asynch")) ram_1 (
    .addr(in_1), .data(ram_1_data), .sel(decoder_1_out0), .ld(R_W));  // open: clr
  RAM #(.addrWidth(10), .bus("asynch")) ram_2 (
    .addr(in_1), .data(ram_1_data), .sel(decoder_1_out1), .ld(R_W));  // open: clr
  RAM #(.addrWidth(10), .bus("asynch")) ram_3 (
    .addr(in_1), .data(ram_1_data), .sel(decoder_1_out2), .ld(R_W));  // open: clr
  RAM #(.addrWidth(10), .bus("asynch")) ram_4 (
    .addr(in_1), .data(ram_1_data), .sel(decoder_1_out3), .ld(R_W));  // open: clr
  RAM #(.addrWidth(10), .bus("asynch")) ram_5 (
    .addr(in_1), .data(ram_5_data), .sel(decoder_1_out0), .ld(R_W));  // open: clr
  RAM #(.addrWidth(10), .bus("asynch")) ram_6 (
    .addr(in_1), .data(ram_5_data), .sel(decoder_1_out1), .ld(R_W));  // open: clr
  RAM #(.addrWidth(10), .bus("asynch")) ram_7 (
    .addr(in_1), .data(ram_5_data), .sel(decoder_1_out2), .ld(R_W));  // open: clr
  RAM #(.addrWidth(10), .bus("asynch")) ram_8 (
    .addr(in_1), .data(ram_5_data), .sel(decoder_1_out3), .ld(R_W));  // open: clr
  assign ram_1_data = not_1_out ? Input : 8'bz;  // Controlled_Buffer controlled_buffer_1
  not not_1 (not_1_out, R_W);
  assign High = R_W ? ram_1_data : 8'bz;  // Controlled_Buffer controlled_buffer_2
  assign Low = R_W ? ram_5_data : 8'bz;  // Controlled_Buffer controlled_buffer_3
  assign ram_5_data = not_2_out ? Input_2 : 8'bz;  // Controlled_Buffer controlled_buffer_4
  not not_2 (not_2_out, R_W);

  // Notes on the sheet:
  //   Address
  //   Address
  //   Output
  //   Output
endmodule
