// Logisim project 行波进位的补码加法减法器.circ as structural Verilog: 2 circuits, main circuit main
module main (
  input  \M_1减 ,
  input  B7,
  input  B6,
  input  B5,
  input  in_5,
  input  B3,
  input  in_7,
  input  B1,
  input  in_9,
  input  in_10,
  input  A6,
  input  B4,
  input  in_13,
  input  B2,
  input  A2,
  input  in_16,
  input  \M_0加 ,
  output \溢出 ,
  output S7,
  output S6,
  output S5,
  output out_22,
  output out_23,
  output out_24,
  output out_25,
  output S0
);

  wire fa_1_out_4, fa_2_out_4, fa_3_out_4, fa_4_out_4, fa_5_out_4, fa_6_out_4, fa_7_out_4, fa_8_out_4,
       xor_2_out, xor_3_out, xor_4_out, xor_5_out, xor_6_out, xor_7_out, xor_8_out, xor_9_out;

  xor xor_1 (\溢出 , fa_1_out_4, fa_2_out_4);
  xor xor_2 (xor_2_out, B7, \M_1减 );
  FA fa_1 (.in_1(fa_2_out_4), .in_2(in_10), .in_3(xor_2_out), .out_4(fa_1_out_4), .out_5(S7));
  FA fa_2 (.in_1(fa_3_out_4), .in_2(A6), .in_3(xor_3_out), .out_4(fa_2_out_4), .out_5(S6));
  xor xor_3 (xor_3_out, B6, \M_1减 );
  FA fa_3 (.in_1(fa_4_out_4), .in_2(B4), .in_3(xor_4_out), .out_4(fa_3_out_4), .out_5(S5));
  xor xor_4 (xor_4_out, B5, \M_1减 );
  FA fa_4 (.in_1(fa_5_out_4), .in_2(in_13), .in_3(xor_5_out), .out_4(fa_4_out_4), .out_5(out_22));
  xor xor_5 (xor_5_out, in_5, \M_1减 );
  FA fa_5 (.in_1(fa_6_out_4), .in_2(B2), .in_3(xor_6_out), .out_4(fa_5_out_4), .out_5(out_23));
  xor xor_6 (xor_6_out, B3, \M_1减 );
  FA fa_6 (.in_1(fa_7_out_4), .in_2(A2), .in_3(xor_7_out), .out_4(fa_6_out_4), .out_5(out_24));
  xor xor_7 (xor_7_out, in_7, \M_1减 );
  FA fa_7 (.in_1(fa_8_out_4), .in_2(in_16), .in_3(xor_8_out), .out_4(fa_7_out_4), .out_5(out_25));
  xor xor_8 (xor_8_out, B1, \M_1减 );
  FA fa_8 (.in_1(\M_1减 ), .in_2(\M_0加 ), .in_3(xor_9_out), .out_4(fa_8_out_4), .out_5(S0));
  xor xor_9 (xor_9_out, in_9, \M_1减 );

  // Notes on the sheet:
  //   Cn
  //   Cn-1
  //   A7
  //   A5
  //   S4
  //   A4
  //   S3
  //   A3
  //   S2
  //   S1
  //   A1
  //   B0
  //   M
  //   A0
endmodule

module FA (
  input  in_1,
  input  in_2,
  input  in_3,
  output out_4,
  output out_5
);

  wire and_1_out, and_2_out, xor_1_out;

  and and_1 (and_1_out, in_1, in_2);
  xor xor_1 (xor_1_out, in_1, in_2);
  and and_2 (and_2_out, in_3, xor_1_out);
  or or_1 (out_4, and_1_out, and_2_out);
  xor xor_2 (out_5, xor_1_out, in_3);
endmodule
